# Fritzing sketch schema_1 (saved by Fritzing 0.9.8b)
breadboards: 1

parts:
  Raspberry_Pi_A1 = Raspberry Pi A
  SG1 = Buzzer 12mm [package=buzzer-cmt1603]

nets:
  N1: Raspberry_Pi_A1.GPIO_2, SG1.1
  N2: Raspberry_Pi_A1.GND, SG1.2
